# Fritzing sketch platine_mega (saved by Fritzing 0.9.0b)
perfboards: 1

parts:
  Bauteil2 = Arduino Mega ADK (Rev3)  # not connected
  J1 = female pin header, 8 pins [form="♀ (female)"]
  J2 = female pin header, 8 pins [form="♀ (female)"]
  J3 = female pin header, 8 pins [form="♀ (female)"]
  J4 = female pin header, 8 pins [form="♀ (female)"]
  J5 = female pin header, 8 pins [form="♀ (female)"]
  J7 = female pin header, 2 pins [form="♀ (female)"]  # not connected
  J8 = female pin header, 2 pins [form="♀ (female)"]
  Display = female pin header, 4 pins [form="♀ (female)"]
  R1 = Resistor [tolerance=±5% resistance=10k package=THT]
  R2 = Resistor [tolerance=±5% resistance=10k package=THT]
  J9 = screw terminal, 5 pins
  J10 = screw terminal, 5 pins
  J6 = female pin header, 13 pins [form="♀ (female)"]
  J11 = female pin header, 10 pins [form="♀ (female)"]
  J12 = female pin header, 6 pins [form="♀ (female)"]
  J13 = screw terminal, 7 pins
  J14 = male pin header, 8 pins [form="♂ (male)"]
  R3 = Resistor [tolerance=±5% resistance=10k package=THT]
  R4 = Resistor [tolerance=±5% resistance=10k package=THT]
  R5 = Resistor [tolerance=±5% resistance=10k package=THT]
  R6 = Resistor [tolerance=±5% resistance=10k package=THT]
  R8 = Resistor [tolerance=±5% resistance=10k package=THT]
  R9 = Resistor [tolerance=±5% resistance=10k package=THT]
  R10 = Resistor [tolerance=±5% resistance=10k package=THT]
  R11 = Resistor [tolerance=±5% resistance=10k package=THT]
  J15 = screw terminal, 15 pins
  R12 = Resistor [tolerance=±5% resistance=4.7k package=THT]  # not connected
  J16 = screw terminal, 3 pins

nets:
  N1: J1.pin1, J14.pin1, R6.Pin_1
  N2: J1.pin2, J14.pin2, R5.Pin_1
  N3: J1.pin3, J14.pin3, R4.Pin_1
  N4: J1.pin4, J14.pin4, R3.Pin_1
  N5: J2.pin1, R8.Pin_1, J15.pin13
  N6: J2.pin2, R9.Pin_1, J15.pin9
  N7: J2.pin3, R10.Pin_1, J15.pin5
  N8: J2.pin4, R11.Pin_1, J15.pin1
  N9: J3.pin5, J11.pin1, J12.pin1, J13.pin7, J16.pin1
  N10: J3.pin6, R3.Pin_0
  N11: J4.pin7, Display.pin3
  N12: J4.pin8, Display.pin4
  N13: J5.pin1, R1.Pin_0, J9.pin3
  N14: J5.pin6, R2.Pin_0, J10.pin3
  N15: J8.pin1, J13.pin5
  N16: J8.pin2, J13.pin3
  N17: Display.pin2, J6.pin1
  N18: R1.Pin_1, R2.Pin_1, J9.pin1
  N19: J9.pin5, J10.pin5
  N20: J6.pin2, J11.pin2
  N21: J6.pin3, J11.pin3
  N22: J6.pin4, J11.pin4
  N23: J6.pin5, J11.pin5
  N24: J6.pin6, J11.pin6
  N25: J6.pin7, J11.pin7
  N26: J6.pin8, J11.pin8
  N27: J6.pin9, J11.pin9
  N28: J6.pin10, J12.pin2
  N29: J6.pin11, J12.pin3
  N30: J6.pin12, J12.pin4
  N31: J6.pin13, J12.pin5
  N32: J15.pin3, J15.pin11
  N33: J15.pin7, J15.pin15

notes:
  Display
  Temperatur und feuchtigkeit
  8er Relay
  4er Relay
  X-bee
  Tastatur
  4 analoge eingänge
